# Fritzing sketch Akvarium (saved by Fritzing 0.9.0b)
breadboards: 1

parts:
  Part1 = Arduino Leonardo (Rev3b)
  LCD1 = LCD screen
  R1 = Trimmer Potentiometer [maximum_resistance=10kΩ package=THT]
  K1 = Relay [part_number=FRS1B-S package=THT]  # not connected
  IC1 = Voltage Regulator [package=78xxl]

nets:
  GND: Part1.GND, LCD1.VSS, LCD1.R/W, R1.leg1, IC1.GND
  N1: LCD1.VDD, R1.leg2, IC1.OUT
  N2: LCD1.V0, R1.wiper
