# Fritzing sketch akvarium (saved by Fritzing 0.9.3b)

parts:
  Part1 = Arduino Nano (Rev3.0) (ICSP)
  LCD1 = LCD screen
  DOWN_/_Krmenie = Round Pushbutton
  R1 = Resistor [tolerance=±5% resistance=220 package="0805 [SMD]"]
  M1 = RioRand LM2596
  M2 = Dagu DGServo 9g (Top view) [part_number=RS001B]
  U1 = 2-Channel 5v Relay Shield [package=relay-2ch5v10a]
  LED1 = DUO LED RG [package="5 mm [THT]"]
  LED2 = DUO LED RG [package="5 mm [THT]"]
  UP_/_Filter_15m = Round Pushbutton
  RESET = Round Pushbutton
  ENTER = Round Pushbutton
  R2 = Resistor [tolerance=±5% resistance=220 package="0805 [SMD]"]
  R3 = Resistor [tolerance=±5% resistance=220 package="0805 [SMD]"]
  R4 = Trimmer Potentiometer [maximum_resistance=10kΩ package=THT]
  Part2 = Real Time Clock Module - DS1307 RTC Breakout Board

nets:
  N1: Part1.D2, LCD1.DB7
  N2: Part1.D3, LCD1.DB6
  N3: Part1.D4, LCD1.DB5
  N4: Part1.D5, LCD1.DB4
  N5: Part1.D6, U1.IN2
  N6: Part1.D7, U1.IN1
  N7: Part1.D8, LED1.red_anode
  N8: Part1.D9, LED1.green_anode
  N9: Part1.D10, M2.pulse
  N10: Part1.D11/MOSI, LCD1.E
  N11: Part1.D12/MISO, LCD1.RS
  GND: Part1.GND, LCD1.VSS, LCD1.R/W, LCD1.LED-, DOWN_/_Krmenie.leg1, M1.Pin_4, M2.gnd, U1.GND, UP_/_Filter_15m.leg1, RESET.leg1, ENTER.leg1, R4.leg1, Part2.GND
  N12: Part1.RESET, RESET.leg0
  5V: Part1.5V, LCD1.VDD, R1.Pin_1, M1.Pin_3, M2.vcc, U1.VCC, LED1.common_cathode, LED2.common_cathode, R2.Pin_1, R3.Pin_1, R4.leg2, Part2.5V
  N13: Part1.A7, ENTER.leg0, R2.Pin_0
  N14: Part1.A5, Part2.SCL
  N15: Part1.A4, Part2.SDA
  N16: Part1.A3, LED2.green_anode
  N17: Part1.A2, LED2.red_anode
  N18: Part1.A1, UP_/_Filter_15m.leg0, R3.Pin_0
  N19: Part1.A0, DOWN_/_Krmenie.leg0, R1.Pin_0
  N20: Part1.D13/SCK, LCD1.LED+
  N21: LCD1.V0, R4.wiper
  N22: U1.K2-In, U1.K2-On, U1.JD-GND

custom parts:
  2-Channel 5v Relay Shield: 2 Channel 5v Relay Shield w. 2x SPD-06VDC-SD-C
